// Logisim project lake_processorfinal.circ as structural Verilog: 35 circuits, main circuit main
module main (
  input  in_1
);

  wire ALU_out_13, branches_1_move_pc, CB, CL, CO, FLAGS_c_block, FLAGS_carry, FLAGS_overflow, FLAGS_sign,
       FLAGS_zero, LOAD_STORE_ld, MPC, not_1_out, not_2_out, or_1_out, OVF, SIGN, ZERO;
  wire [3:0] _7ORIG, _11ORIG, _15ORIG, CMD, CU_dest_reg, DEST_REG_out_2, RbREG, RD1, RD2, RDA1, RDB2, RdREG;
  wire [5:0] SET;
  wire [7:0] WR8;
  wire [15:0] _16R1, _16R2, ALU_wr16, BPC, FP, IMD, LOAD_STORE_retrieval_m_position, multiplexer_1_out, NFP,
       NPC, NRa, NRb, OD, PC, ram_1_data, REGISTERS_r1, REGISTERS_r2, REGISTERS_r3;

  not not_1 (not_1_out, or_1_out);
  BRANCHES branches_1 (
    .RDBr(_16R1), .CMD({_15ORIG, _11ORIG, _7ORIG, CMD}), .S(SIGN), .Z(ZERO), .O(OVF), .C(CO), .CB(CB),
    .PC(PC), .PC_PLACE(BPC), .MOVE_PC(branches_1_move_pc));
  or or_1 (or_1_out, branches_1_move_pc, MPC);
  Counter #(.width(16), .max('hffff)) counter_1 (
    .load(or_1_out), .D(NPC), .count(not_1_out), .Q(PC), .clk(CL), .clr(in_1));  // open: carry
  Clock clock_1 (.out(CL));
  ROM #(.addrWidth(16), .dataWidth(16)) rom_1 (.addr(PC), .data({_15ORIG, _11ORIG, _7ORIG, CMD}), .sel(1'b1));
  CU CU (
    .in_1({_15ORIG, _11ORIG, _7ORIG, CMD}), .READB2(RDB2), .READA1(RDA1), .SETLO_HI(SET), .SETBITS(WR8),
    .DEST_REG(CU_dest_reg));  // open: out_2
  DotMatrix #(.matrixrows(1)) dotmatrix_1 (
    .col0(FLAGS_sign), .col1(FLAGS_zero), .col2(FLAGS_overflow), .col3(FLAGS_carry), .col4(FLAGS_c_block));
  Flags FLAGS (
    .in_1({_15ORIG, _11ORIG, _7ORIG, CMD}), .CLOCK(CL), .in_2(SIGN), .in_3(ZERO), .in_4(OVF), .in_5(CO),
    .in_6(CB), .SIGN(FLAGS_sign), .ZERO(FLAGS_zero), .OVERFLOW(FLAGS_overflow), .CARRY(FLAGS_carry),
    .C_BLOCK(FLAGS_c_block));
  DEST_REG DEST_REG (.SET_HI_AND_3DRESS(CU_dest_reg), .out_2(DEST_REG_out_2));
  ALU ALU (
    .READ_1_B(_16R1), .READ_2_A(_16R2), ._12_15BITS(_15ORIG), .WR16(ALU_wr16), .out_13(ALU_out_13),
    .SIGN(FLAGS_sign), .ZERO(FLAGS_zero), .OVERFLOW(FLAGS_overflow), .CARRY_IN(FLAGS_carry),
    .CARRY_BLOCK(FLAGS_c_block), .SIGN_2(SIGN), .ZERO_2(ZERO), .OVERFLOW_2(OVF), .CARRY_OUT(CO),
    .CARRY_BLOCK_2(CB), .LDRESULT(OD));
  Multiplexer #(.width(16)) multiplexer_1 (
    .in0(ALU_wr16), .in1(OD), .out(multiplexer_1_out), .sel(ALU_out_13));  // open: en
  LOAD_STORE LOAD_STORE (
    .Rb_DATA(_16R1), .COMMAND({_15ORIG, _11ORIG, _7ORIG, CMD}), .INPUT_MEMORY_DATA(IMD), .Rd_DATA(_16R2),
    .CLOCK(CL), .Rb_REGISTER(RbREG), .Rd_REGISTER(RdREG),
    .retrieval_M_position(LOAD_STORE_retrieval_m_position), .LD(LOAD_STORE_ld), .OUTPUT_DATA(OD));  // open: S_L, OUTPUT_M_LOC
  CALL_RETURN call_return_1 (
    .Rb(_16R1), .Ra(_16R2), .FP(FP), .PC(PC), .CHANGE_PC(BPC), .Rb_2(NRb), .Ra_2(NRa), .FP_2(NFP), .NPC(NPC),
    .MOVE_PC(MPC), ._15ORIG(_15ORIG));
  Register_File REGISTERS (
    .WR16(multiplexer_1_out), .RDSel2(RD2), .RDSel1(RD1), .DEST_REG(DEST_REG_out_2), .WR8(WR8),
    .HI_LO_AND_16_8(SET), .RbCALL_RET(NRb), .RaCALL_RET(NRa), .FPCALL_RET(NFP), .CLOCK(CL),
    .R1(REGISTERS_r1), .R2(REGISTERS_r2), .R3(REGISTERS_r3), .RD1(_16R1), .RD2(_16R2), .FP(FP));
  // Probe on REGISTERS_r1
  // Probe on REGISTERS_r2
  // Probe on REGISTERS_r3
  RDregisterSEL RDregisterSEL (
    .RDSEL1(RDB2), .RDSEL2(RDA1), .RbREG(RbREG), .RdREG(RdREG), ._7ORIG(_7ORIG), ._12_15ORIG(_15ORIG),
    .RDSEL1_2(RD1), .RDSEL2_2(RD2));
  not not_2 (not_2_out, LOAD_STORE_ld);
  Multiplexer #(.width(16)) multiplexer_2 (.in1(ram_1_data), .out(IMD), .sel(LOAD_STORE_ld));  // open: in0, en
  RAM #(.addrWidth(16), .dataWidth(16)) ram_1 (
    .addr(LOAD_STORE_retrieval_m_position), .data(ram_1_data), .clk(CL), .ld(LOAD_STORE_ld));  // open: sel, clr
  Multiplexer #(.width(16)) multiplexer_3 (.in1(OD), .out(ram_1_data), .sel(not_2_out));  // open: in0, en

  // Other names for the same wires on the sheet: CMD[15:4] = {_15ORIG, _11ORIG, _7ORIG}

  // Notes on the sheet:
  //   contents of rom_1 (hex, n*v repeats v):
  //   e103 f101 6100 4203 a312 b112 b112 3861 3061 3062 e40e 1804 0 0 e413 1c04 e519 e205 2121 e110 f100
  //   e202 2021 0 0 fab0
endmodule

module CU (
  input  [15:0] in_1,
  output [15:0] out_2,
  output [3:0] READB2,
  output [3:0] READA1,
  output [5:0] SETLO_HI,
  output [7:0] SETBITS,
  output [3:0] DEST_REG
);

  wire [3:0] _8_11BITS_out_4, _8_11BITS_out_5, _15MOD;

  _12_15BITS _12_15BITS (._12_15BITS(in_1[15:12]), .out_2(_15MOD));
  _8_11BITS _8_11BITS (
    ._12_15ORIG(in_1[15:12]), ._8_11BITS(in_1[11:8]), ._12_15BITS_SORTED(_15MOD), .out_4(_8_11BITS_out_4),
    .out_5(_8_11BITS_out_5), .out_6(DEST_REG));
  _4_7BITS _4_7BITS (
    ._12_15ORIG(in_1[15:12]), ._8_11ORIG(in_1[11:8]), ._4_7BITS(in_1[7:4]), ._12_15BITS_SORTED(_15MOD),
    .READA(READA1), .SETLO_HI(SETBITS[7:4]));
  _0_3BITS _0_3BITS (
    ._12_15ORIG(in_1[15:12]), ._8_11ORIG(in_1[11:8]), ._0_3BITS(in_1[3:0]), ._12_15BITS_SORTED(_15MOD),
    .READB(READB2), .SETLO_HI(SETBITS[3:0]));
  SETLO_HICHOSE setlo_hichose_1 (._12_15MOD(_15MOD), .bit8(in_1[8]), ._15BITS(in_1[15:12]), .out_4(SETLO_HI));

  // Other names for the same wires on the sheet: _3ORIG[3:0] = in_1[3:0]; _7ORIG[3:0] = in_1[7:4];
  //   _11ORIG[3:0] = in_1[11:8]; _15ORIG[3:0] = in_1[15:12]; _0_3SET[3:0] = SETBITS[3:0]; _4_7SET[3:0] = SETBITS[7:4]
endmodule

module _12_15BITS (
  input  [3:0] _12_15BITS,
  output [3:0] out_2
);

  wire decoder_1_out0, decoder_1_out1, decoder_1_out2, decoder_1_out3, decoder_1_out4, decoder_1_out5,
       decoder_1_out6, decoder_1_out7, decoder_1_out8, decoder_1_out9, decoder_1_out10, decoder_1_out11,
       decoder_1_out12, decoder_1_out13, decoder_1_out14, decoder_1_out15;

  Decoder #(.select(4)) decoder_1 (
    .out0(decoder_1_out0), .out1(decoder_1_out1), .out2(decoder_1_out2), .out3(decoder_1_out3),
    .out4(decoder_1_out4), .out5(decoder_1_out5), .out6(decoder_1_out6), .out7(decoder_1_out7),
    .out8(decoder_1_out8), .out9(decoder_1_out9), .out10(decoder_1_out10), .out11(decoder_1_out11),
    .out12(decoder_1_out12), .out13(decoder_1_out13), .out14(decoder_1_out14), .out15(decoder_1_out15),
    .sel(_12_15BITS));  // open: en
  or ALL_OTHER (out_2[0], decoder_1_out0, decoder_1_out1, decoder_1_out2, decoder_1_out3);
  or LOAD_STORE (out_2[1], decoder_1_out4, decoder_1_out5, decoder_1_out6, decoder_1_out7);
  or _3_ADDRESS_OPS (out_2[2], decoder_1_out8, decoder_1_out9, decoder_1_out10, decoder_1_out11, decoder_1_out12, decoder_1_out13);
  or SET (out_2[3], decoder_1_out14, decoder_1_out15);

  // Notes on the sheet:
  //   ALLOWS 12-15 BITS TO TELL OTHER BITS WHAT TO DO:
endmodule

module _8_11BITS (
  input  [3:0] _12_15ORIG,
  input  [3:0] _8_11BITS,
  input  [3:0] _12_15BITS_SORTED,
  output [3:0] out_4,
  output [3:0] out_5,
  output [3:0] out_6
);

  wire and_1_out, and_2_out;
  wire [2:1] and_3_out;

  and and_1 (and_1_out, ~_12_15ORIG[0], ~_12_15ORIG[1], _12_15ORIG[2], ~_12_15ORIG[3]);  // AND_Gate
  and and_2 (and_2_out, ~_12_15ORIG[1], _12_15BITS_SORTED[1]);  // AND_Gate
  and and_3 (and_3_out[1], ~and_1_out, _12_15BITS_SORTED[1]);  // AND_Gate
  or or_1 (and_3_out[2], and_2_out, _12_15BITS_SORTED[2], _12_15BITS_SORTED[3], and_1_out);
  Demultiplexer #(.select(3), .width(4)) demultiplexer_1 (
    .out1(out_4), .out2(out_5), .out4(out_6), .in(_8_11BITS), .sel({and_3_out, _12_15BITS_SORTED[0]}));  // open: out0, out3, out5, out6, out7, en

  // Notes on the sheet:
  //   WHAT TO DO WITH THE 8-11 BITS:
  //   both b15:14 11 and 10 send 8-11 bits to the same place
endmodule

module _4_7BITS (
  input  [3:0] _12_15ORIG,
  input  [3:0] _8_11ORIG,
  input  [3:0] _4_7BITS,
  input  [3:0] _12_15BITS_SORTED,
  output [3:0] READA,
  output [3:0] SETLO_HI
);

  Demultiplexer #(.select(4), .width(4)) demultiplexer_1 (
    .out4(READA), .out8(SETLO_HI), .in(_4_7BITS), .sel(_12_15BITS_SORTED));  // open: out0, out1, out2, out3, out5, out6, out7, out9, out10, out11, out12, out13, out14, out15, en

  // Notes on the sheet:
  //   WHAT TO DO WITH THE 4-7 BITS:
endmodule

module _0_3BITS (
  input  [3:0] _12_15ORIG,
  input  [3:0] _8_11ORIG,
  input  [3:0] _0_3BITS,
  input  [3:0] _12_15BITS_SORTED,
  output [3:0] READB,
  output [3:0] SETLO_HI
);

  Demultiplexer #(.select(4), .width(4)) demultiplexer_1 (
    .out4(READB), .out8(SETLO_HI), .in(_0_3BITS), .sel(_12_15BITS_SORTED));  // open: out0, out1, out2, out3, out5, out6, out7, out9, out10, out11, out12, out13, out14, out15, en

  // Notes on the sheet:
  //   WHAT TO DO WITH THE 0-3 BITS:
endmodule

// SETLO/HI
module SETLO_HICHOSE (
  input  [3:0] _12_15MOD,
  input  bit8,
  input  [3:0] _15BITS,
  output [5:0] out_4
);

  Multiplexer multiplexer_1 (.in0(1'b0), .in1(1'b1), .out(out_4[0]), .sel(_12_15MOD[3]));  // open: en

  assign out_4[5:1] = {bit8, _15BITS};
endmodule

module DEST_REG (
  input  [3:0] SET_HI_AND_3DRESS,
  output [3:0] out_2
);


  assign out_2 = SET_HI_AND_3DRESS;
endmodule

module Flags (
  input  [15:0] in_1,
  input  in_2,
  input  in_3,
  input  in_4,
  input  in_5,
  input  in_6,
  input  CLOCK,
  output SIGN,
  output ZERO,
  output OVERFLOW,
  output CARRY,
  output C_BLOCK
);

  wire and_1_out, and_2_out, and_3_out, and_4_out, and_5_out, and_6_out, and_7_out, and_8_out, and_9_out,
       and_10_out, and_11_out, and_12_out, and_13_out, and_14_out, and_15_out, and_16_out, and_17_out,
       multiplexer_2_out, or_1_out, or_2_out, or_3_out, or_4_out, or_5_out;
  wire [4:0] multiplexer_1_out;

  and and_1 (and_1_out, ~in_1[4], in_1[5], in_1[6], ~in_1[7], ~in_1[9], ~in_1[10], in_1[12], in_1[13], ~in_1[14], ~in_1[15]);  // AND_Gate
  Multiplexer #(.width(5)) multiplexer_1 (
    .in0({5{1'b0}}), .in1({in_1[8], in_1[3:0]}), .out(multiplexer_1_out), .sel(and_1_out));  // open: en
  Multiplexer multiplexer_2 (.in0(1'b0), .in1(in_1[11]), .out(multiplexer_2_out), .sel(and_2_out));  // open: en
  and and_2 (and_2_out, and_1_out, in_1[11]);
  and and_3 (and_3_out, ~multiplexer_2_out, multiplexer_1_out[0]);  // AND_Gate
  and and_4 (and_4_out, multiplexer_2_out, multiplexer_1_out[0]);
  or or_1 (or_1_out, and_3_out, in_2);
  and and_5 (and_5_out, ~and_4_out, or_1_out);  // AND_Gate
  and and_6 (and_6_out, ~multiplexer_2_out, multiplexer_1_out[1]);  // AND_Gate
  and and_7 (and_7_out, multiplexer_2_out, multiplexer_1_out[1]);
  or or_2 (or_2_out, and_6_out, in_3);
  and and_8 (and_8_out, ~and_7_out, or_2_out);  // AND_Gate
  D_Flip_Flop d_ff_1 (.clk(CLOCK), .D(and_5_out), .Q(SIGN));  // open: Qn, preset, en, reset
  and and_9 (and_9_out, ~multiplexer_2_out, multiplexer_1_out[2]);  // AND_Gate
  and and_10 (and_10_out, multiplexer_2_out, multiplexer_1_out[2]);
  or or_3 (or_3_out, and_9_out, in_4);
  and and_11 (and_11_out, ~and_10_out, or_3_out);  // AND_Gate
  D_Flip_Flop d_ff_2 (.clk(CLOCK), .D(and_8_out), .Q(ZERO));  // open: Qn, preset, en, reset
  and and_12 (and_12_out, ~multiplexer_2_out, multiplexer_1_out[3]);  // AND_Gate
  and and_13 (and_13_out, multiplexer_2_out, multiplexer_1_out[3]);
  or or_4 (or_4_out, and_12_out, in_5);
  and and_14 (and_14_out, ~and_13_out, or_4_out);  // AND_Gate
  D_Flip_Flop d_ff_3 (.clk(CLOCK), .D(and_11_out), .Q(OVERFLOW));  // open: Qn, preset, en, reset
  and and_15 (and_15_out, ~multiplexer_2_out, multiplexer_1_out[4]);  // AND_Gate
  and and_16 (and_16_out, multiplexer_2_out, multiplexer_1_out[4]);
  or or_5 (or_5_out, and_15_out, in_6);
  and and_17 (and_17_out, ~and_16_out, or_5_out);  // AND_Gate
  D_Flip_Flop d_ff_4 (.clk(CLOCK), .D(and_14_out), .Q(CARRY));  // open: Qn, preset, en, reset
  D_Flip_Flop d_ff_5 (.clk(CLOCK), .D(and_17_out), .Q(C_BLOCK));  // open: Qn, preset, en, reset

  // Notes on the sheet:
  //   SET
  //   CLEAR
endmodule

module ALU (
  input  CARRY_IN,
  input  CARRY_BLOCK,
  input  [15:0] READ_1_B,
  input  [15:0] READ_2_A,
  input  OVERFLOW,
  input  SIGN,
  input  ZERO,
  input  [3:0] _12_15BITS,
  input  [15:0] LDRESULT,
  output [15:0] WR16,
  output OVERFLOW_2,
  output CARRY_BLOCK_2,
  output out_13,
  output SIGN_2,
  output ZERO_2,
  output CARRY_OUT
);

  wire ADD_SUB, Arth, decoder_1_out9, decoder_1_out12, decoder_1_out13, decoder_1_out14, decoder_1_out15,
       loadf_1_ls, loadf_1_lz, NS, signed_add_sub_1_carry_out;
  wire [2:0] decoder_1_out8;
  wire [15:0] AND_out_3, signed_add_sub_1_out_7;

  SIGN sign_1 (.RESULT(WR16), .NS(NS), .Arth(Arth), .SIGN(SIGN), .SIGN_2(SIGN_2), .LS(loadf_1_ls));
  OF of_1 (.in_3(WR16), .in_1(READ_2_A), .in_2(READ_1_B), .in_5(OVERFLOW), .out_6(OVERFLOW_2), .in_4(ADD_SUB));
  ZERO zero_1 (.RESULT(WR16), .NS(NS), .Arth(Arth), .ZERO(ZERO), .ZERO_2(ZERO_2), .LZ(loadf_1_lz));
  LOADF loadf_1 (._15ORIG(_12_15BITS), .LOADRESULT(LDRESULT), .LS(loadf_1_ls), .LZ(loadf_1_lz));
  AND AND (.in_1(READ_1_B), .in_2(READ_2_A), .out_3(AND_out_3));
  SIGNED_ADD_SUB signed_add_sub_1 (
    .ADD_SUB(_12_15BITS[0]), ._4_Bit_input__1(READ_2_A), ._4_Bit_input__2(READ_1_B), .C(CARRY_IN),
    .CB(CARRY_BLOCK), .Carry_Out(signed_add_sub_1_carry_out), .out_7(signed_add_sub_1_out_7));
  Decoder #(.select(4)) decoder_1 (
    .out8(decoder_1_out8[0]), .out9(decoder_1_out9), .out10(decoder_1_out8[1]), .out11(decoder_1_out8[2]),
    .out12(decoder_1_out12), .out13(decoder_1_out13), .out14(decoder_1_out14), .out15(decoder_1_out15),
    .sel(_12_15BITS));  // open: out0, out1, out2, out3, out4, out5, out6, out7, en
  not not_1 (out_13, _12_15BITS[3]);
  and and_2 (NS, decoder_1_out14, decoder_1_out15, ~decoder_1_out12);  // AND_Gate
  Multiplexer #(.select(3), .width(16)) multiplexer_1 (
    .in1(AND_out_3), .in2(signed_add_sub_1_out_7), .in4(signed_add_sub_1_out_7), .out(WR16),
    .sel(decoder_1_out8));  // open: in0, in3, in5, in6, in7, en
  or or_1 (ADD_SUB, decoder_1_out8[2], decoder_1_out8[1]);
  and and_3 (CARRY_OUT, ADD_SUB, signed_add_sub_1_carry_out);
  or or_2 (Arth, decoder_1_out8[0], decoder_1_out9, decoder_1_out8[1], decoder_1_out8[2], decoder_1_out12, decoder_1_out13);

  assign CARRY_BLOCK_2 = CARRY_BLOCK;

  // Other names for the same wires on the sheet: _15ORIG[3:0] = _12_15BITS; BIT12 = _12_15BITS[0];
  //   result[15:0] = WR16
endmodule

module ADD (
  input  in_1,
  input  in_2,
  input  [15:0] in_3,
  input  [15:0] in_4,
  output [15:0] out_5,
  output out_6
);

  wire and_1_out;

  and and_1 (and_1_out, in_1, ~in_2);  // AND_Gate
  Adder #(.width(16)) adder_1 (.a(in_3), .b(in_4), .out(out_5), .cin(and_1_out), .cout(out_6));
endmodule

module SUB (
  input  in_1,
  input  in_2,
  input  [15:0] in_3,
  input  [15:0] in_4,
  output [15:0] out_5,
  output out_6
);

  wire and_1_out;

  and and_1 (and_1_out, ~in_1, ~in_2);  // AND_Gate
  Subtractor #(.width(16)) subtractor_1 (.a(in_3), .b(in_4), .out(out_5), .bin(and_1_out), .bout(out_6));
endmodule

module AND (
  input  [15:0] in_1,
  input  [15:0] in_2,
  output [15:0] out_3
);

  HALFAND halfand_1 (
    .in_1(in_1[0]), .in_2(in_2[0]), .in_3(in_1[1]), .in_4(in_2[1]), .in_5(in_1[2]), .in_6(in_2[2]),
    .in_7(in_1[3]), .in_8(in_2[3]), .in_9(in_1[4]), .in_10(in_2[4]), .in_11(in_1[5]), .in_12(in_2[5]),
    .in_13(in_1[6]), .in_14(in_2[6]), .in_15(in_1[7]), .in_16(in_2[7]), .out_17(out_3[7:0]));
  HALFAND halfand_2 (
    .in_1(in_1[8]), .in_2(in_2[8]), .in_3(in_1[9]), .in_4(in_2[9]), .in_5(in_1[10]), .in_6(in_2[10]),
    .in_7(in_1[11]), .in_8(in_2[11]), .in_9(in_1[12]), .in_10(in_2[12]), .in_11(in_1[13]), .in_12(in_2[13]),
    .in_13(in_1[14]), .in_14(in_2[14]), .in_15(in_1[15]), .in_16(in_2[15]), .out_17(out_3[15:8]));
endmodule

module HALFAND (
  input  in_1,
  input  in_2,
  input  in_3,
  input  in_4,
  input  in_5,
  input  in_6,
  input  in_7,
  input  in_8,
  input  in_9,
  input  in_10,
  input  in_11,
  input  in_12,
  input  in_13,
  input  in_14,
  input  in_15,
  input  in_16,
  output [7:0] out_17
);

  and and_1 (out_17[0], in_1, in_2);
  and and_2 (out_17[1], in_3, in_4);
  and and_3 (out_17[2], in_5, in_6);
  and and_4 (out_17[3], in_7, in_8);
  and and_5 (out_17[4], in_9, in_10);
  and and_6 (out_17[5], in_11, in_12);
  and and_7 (out_17[6], in_13, in_14);
  and and_8 (out_17[7], in_15, in_16);
endmodule

// CALL & RET
module CALL_RETURN (
  input  [15:0] Rb,
  input  [15:0] Ra,
  input  [15:0] FP,
  input  [15:0] PC,
  input  [15:0] CHANGE_PC,
  input  [3:0] _15ORIG,
  output [15:0] Rb_2,
  output [15:0] Ra_2,
  output [15:0] FP_2,
  output [15:0] NPC,
  output MOVE_PC
);

  Adder #(.width(16)) adder_1 (.a(16'h1), .b(PC), .out(Rb_2));  // open: cin, cout
  Multiplexer #(.width(16)) multiplexer_1 (.in0(CHANGE_PC), .in1(Rb), .out(NPC), .sel(_15ORIG[1]));  // open: en
  and and_1 (MOVE_PC, ~_15ORIG[0], _15ORIG[1], ~_15ORIG[2], ~_15ORIG[3]);  // AND_Gate

  assign FP_2 = Ra;
  assign Ra_2 = FP;
endmodule

module Register_File (
  input  [15:0] WR16,
  input  CLOCK,
  input  [3:0] RDSel2,
  input  [3:0] RDSel1,
  input  [3:0] DEST_REG,
  input  [7:0] WR8,
  input  [5:0] HI_LO_AND_16_8,
  input  [15:0] RbCALL_RET,
  input  [15:0] RaCALL_RET,
  input  [15:0] FPCALL_RET,
  output [15:0] R1,
  output [15:0] R2,
  output [15:0] R3,
  output [15:0] RD1,
  output [15:0] RD2,
  output [15:0] FP
);

  wire decoder_1_out0, decoder_1_out1, decoder_1_out2, decoder_1_out3, decoder_1_out4, decoder_1_out5,
       decoder_1_out6, decoder_1_out7, decoder_1_out8, decoder_1_out9, decoder_1_out10, decoder_1_out11,
       decoder_1_out12, decoder_1_out13, decoder_1_out14, decoder_1_out15;
  wire [15:0] R0_R7_out_16, R0_R7_out_20, R0_R7_out_21, R0_R7_out_22, R0_R7_out_23, R8_R15_out_17,
       R8_R15_out_18, R8_R15_out_19, R8_R15_out_20, R8_R15_out_21, R8_R15_out_22, R8_R15_out_24;

  Decoder #(.select(4)) decoder_1 (
    .out0(decoder_1_out0), .out1(decoder_1_out1), .out2(decoder_1_out2), .out3(decoder_1_out3),
    .out4(decoder_1_out4), .out5(decoder_1_out5), .out6(decoder_1_out6), .out7(decoder_1_out7),
    .out8(decoder_1_out8), .out9(decoder_1_out9), .out10(decoder_1_out10), .out11(decoder_1_out11),
    .out12(decoder_1_out12), .out13(decoder_1_out13), .out14(decoder_1_out14), .out15(decoder_1_out15),
    .sel(DEST_REG));  // open: en
  R0_R7 R0_R7 (
    .LO_HI(WR8), ._16(WR16), .SEL(HI_LO_AND_16_8), .R0(decoder_1_out0), .R1(decoder_1_out1),
    .R2(decoder_1_out2), .R3(decoder_1_out3), .R4(decoder_1_out4), .R5(decoder_1_out5), .R6(decoder_1_out6),
    .R7(decoder_1_out7), .RbCALL_RET(RbCALL_RET), .RaCALL_RET(RaCALL_RET), .Rb_AND_Ra({RDSel2, RDSel1}),
    .CLOCK(CLOCK), .out_16(R0_R7_out_16), .out_17(R1), .out_18(R2), .out_19(R3), .out_20(R0_R7_out_20),
    .out_21(R0_R7_out_21), .out_22(R0_R7_out_22), .out_23(R0_R7_out_23));
  R8_R15 R8_R15 (
    .LO_HI(WR8), ._16(WR16), .SEL(HI_LO_AND_16_8), .R8(decoder_1_out8), .R9(decoder_1_out9),
    .R10(decoder_1_out10), .R11(decoder_1_out11), .R12(decoder_1_out12), .R13(decoder_1_out13),
    .R14(decoder_1_out14), .R15(decoder_1_out15), .RbCALL_RET(RbCALL_RET), .RaCALL_RET(RaCALL_RET),
    .FPCALL_RET(FPCALL_RET), .Rb_AND_Ra({RDSel2, RDSel1}), .CLOCK(CLOCK), .out_17(R8_R15_out_17),
    .out_18(R8_R15_out_18), .out_19(R8_R15_out_19), .out_20(R8_R15_out_20), .out_21(R8_R15_out_21),
    .out_22(R8_R15_out_22), .out_23(FP), .out_24(R8_R15_out_24));
  Multiplexer #(.select(4), .width(16)) multiplexer_1 (
    .in0(R0_R7_out_16), .in1(R1), .in2(R2), .in3(R3), .in4(R0_R7_out_20), .in5(R0_R7_out_21),
    .in6(R0_R7_out_22), .in7(R0_R7_out_23), .in8(R8_R15_out_17), .in9(R8_R15_out_18), .in10(R8_R15_out_19),
    .in11(R8_R15_out_20), .in12(R8_R15_out_21), .in13(R8_R15_out_22), .in14(FP), .in15(R8_R15_out_24),
    .out(RD1), .sel(RDSel1));  // open: en
  Multiplexer #(.select(4), .width(16)) multiplexer_2 (
    .in0(R0_R7_out_16), .in1(R1), .in2(R2), .in3(R3), .in4(R0_R7_out_20), .in5(R0_R7_out_21),
    .in6(R0_R7_out_22), .in7(R0_R7_out_23), .in8(R8_R15_out_17), .in9(R8_R15_out_18), .in10(R8_R15_out_19),
    .in11(R8_R15_out_20), .in12(R8_R15_out_21), .in13(R8_R15_out_22), .in14(FP), .in15(R8_R15_out_24),
    .out(RD2), .sel(RDSel2));  // open: en

  // Other names for the same wires on the sheet: Rb_AND_Ra[7:0] = {RDSel2, RDSel1}
endmodule

module _8_16_bit_register (
  input  [7:0] HI_LO,
  input  [15:0] _16,
  input  [5:0] HI_LO_AND_16_8,
  input  CLOCK,
  input  [15:0] RbCALL_RET,
  input  [15:0] RaCALL_RET,
  input  Rb,
  input  Rd,
  input  ENABLE,
  output [15:0] out_10
);

  wire and_2_out, and_3_out, and_4_out, or_1_out;
  wire [0:0] and_1_out, not_1_out;
  wire [1:0] multiplexer_1_out, multiplexer_2_out;
  wire [7:0] multiplexer_4_out, multiplexer_5_out;
  wire [15:0] multiplexer_3_out;

  and and_1 (and_1_out[0], ~HI_LO_AND_16_8[5], Rb);  // AND_Gate
  not not_1 (not_1_out[0], HI_LO_AND_16_8[1]);
  and and_2 (and_2_out, ~HI_LO_AND_16_8[1], HI_LO_AND_16_8[2], ~HI_LO_AND_16_8[3], ~HI_LO_AND_16_8[4]);  // AND_Gate
  Multiplexer #(.width(2)) multiplexer_1 (
    .in0(2'b00), .in1({Rd, and_1_out[0]}), .out(multiplexer_1_out), .sel(and_2_out));  // open: en
  // Probe on multiplexer_1_out
  Multiplexer #(.width(2)) multiplexer_2 (
    .in0(2'b11), .in1({HI_LO_AND_16_8[1], not_1_out[0]}), .out(multiplexer_2_out), .sel(HI_LO_AND_16_8[0]));  // open: en
  Multiplexer #(.select(2), .width(16)) multiplexer_3 (
    .in0(_16), .in1(RbCALL_RET), .in2(RaCALL_RET), .out(multiplexer_3_out), .sel(multiplexer_1_out));  // open: in3, en
  Multiplexer #(.width(8)) multiplexer_4 (
    .in0(multiplexer_3_out[7:0]), .in1(HI_LO), .out(multiplexer_4_out), .sel(HI_LO_AND_16_8[0]),
    .en(multiplexer_2_out[0]));
  and and_3 (and_3_out, and_2_out, Rd);
  Register LO (.D(multiplexer_4_out), .en(or_1_out), .Q(out_10[7:0]), .clk(CLOCK));  // open: clr
  Register HI (.D(multiplexer_5_out), .en(or_1_out), .Q(out_10[15:8]), .clk(CLOCK));  // open: clr
  Multiplexer #(.width(8)) multiplexer_5 (
    .in0(multiplexer_3_out[15:8]), .in1(HI_LO), .out(multiplexer_5_out), .sel(HI_LO_AND_16_8[0]),
    .en(multiplexer_2_out[1]));
  and and_4 (and_4_out, and_2_out, and_1_out[0]);
  or or_1 (or_1_out, and_4_out, and_3_out, ENABLE);

  // Notes on the sheet:
  //   CALL/RET
  //   15ORIG
  //   LO
  //   HI
endmodule

module FPReg (
  input  [7:0] HI_LO,
  input  [15:0] _16,
  input  [5:0] HI_LO_AND_16_8,
  input  CLOCK,
  input  [15:0] NEWFP,
  input  ENABLE,
  output [15:0] out_7
);

  wire and_1_out, not_1_out, or_1_out;
  wire [7:0] multiplexer_1_out, multiplexer_3_out;
  wire [15:0] multiplexer_2_out;

  and and_1 (and_1_out, ~HI_LO_AND_16_8[1], HI_LO_AND_16_8[2], ~HI_LO_AND_16_8[3], ~HI_LO_AND_16_8[4]);  // AND_Gate
  or or_1 (or_1_out, and_1_out, ENABLE);
  Multiplexer #(.width(8)) multiplexer_1 (
    .in0(multiplexer_2_out[7:0]), .in1(HI_LO), .out(multiplexer_1_out), .sel(HI_LO_AND_16_8[0]),
    .en(not_1_out));
  not not_1 (not_1_out, HI_LO_AND_16_8[1]);
  Multiplexer #(.width(16)) multiplexer_2 (
    .in0(_16), .in1(NEWFP), .out(multiplexer_2_out), .sel(and_1_out));  // open: en
  Multiplexer #(.width(8)) multiplexer_3 (
    .in0(multiplexer_2_out[15:8]), .in1(HI_LO), .out(multiplexer_3_out), .sel(HI_LO_AND_16_8[0]),
    .en(HI_LO_AND_16_8[1]));
  Register LO (.D(multiplexer_1_out), .en(or_1_out), .Q(out_7[7:0]), .clk(CLOCK));  // open: clr
  Register HI (.D(multiplexer_3_out), .en(or_1_out), .Q(out_7[15:8]), .clk(CLOCK));  // open: clr

  // Notes on the sheet:
  //   15ORIG
  //   LO
  //   HI
endmodule

module R0_R7 (
  input  [7:0] LO_HI,
  input  [15:0] _16,
  input  [5:0] SEL,
  input  R0,
  input  R1,
  input  R2,
  input  R3,
  input  R4,
  input  R5,
  input  R6,
  input  R7,
  input  [15:0] RbCALL_RET,
  input  CLOCK,
  input  [15:0] RaCALL_RET,
  input  [7:0] Rb_AND_Ra,
  output [15:0] out_16,
  output [15:0] out_17,
  output [15:0] out_18,
  output [15:0] out_19,
  output [15:0] out_20,
  output [15:0] out_21,
  output [15:0] out_22,
  output [15:0] out_23
);

  R0_R3 R0_R3 (
    .LO_HI(LO_HI), ._16(_16), .SEL(SEL), .R0(R0), .R1(R1), .R2(R2), .R3(R3), .RbCALL_RET(RbCALL_RET),
    .RaCALL_RET(RaCALL_RET), .Rb_AND_Ra(Rb_AND_Ra), .CLOCK(CLOCK), .R0_2(out_16), .R1_2(out_17),
    .R2_2(out_18), .R3_2(out_19));
  R4_R7 R4_R7 (
    .LO_HI(LO_HI), ._16(_16), .SEL(SEL), .R4(R4), .R5(R5), .R6(R6), .R7(R7), .RbCALL_RET(RbCALL_RET),
    .RaCALL_RET(RaCALL_RET), .Rb_AND_Ra(Rb_AND_Ra), .CLOCK(CLOCK), .out_12(out_20), .out_13(out_21),
    .out_14(out_22), .out_15(out_23));
endmodule

module R0_R3 (
  input  [7:0] LO_HI,
  input  [15:0] _16,
  input  [5:0] SEL,
  input  R0,
  input  R1,
  input  R2,
  input  R3,
  input  CLOCK,
  input  [15:0] RbCALL_RET,
  input  [15:0] RaCALL_RET,
  input  [7:0] Rb_AND_Ra,
  output [15:0] R0_2,
  output [15:0] R1_2,
  output [15:0] R2_2,
  output [15:0] R3_2
);

  wire decoder_1_out0, decoder_1_out1, decoder_1_out2, decoder_1_out3, decoder_2_out0, decoder_2_out1,
       decoder_2_out2, decoder_2_out3;

  Decoder #(.select(4)) decoder_1 (
    .out0(decoder_1_out0), .out1(decoder_1_out1), .out2(decoder_1_out2), .out3(decoder_1_out3),
    .sel(Rb_AND_Ra[3:0]));  // open: out4, out5, out6, out7, out8, out9, out10, out11, out12, out13, out14, out15, en
  Decoder #(.select(4)) decoder_2 (
    .out0(decoder_2_out0), .out1(decoder_2_out1), .out2(decoder_2_out2), .out3(decoder_2_out3),
    .sel(Rb_AND_Ra[7:4]));  // open: out4, out5, out6, out7, out8, out9, out10, out11, out12, out13, out14, out15, en
  _8_16_bit_register u_R0 (
    .HI_LO(LO_HI), ._16(_16), .HI_LO_AND_16_8(SEL), .RbCALL_RET(RbCALL_RET), .RaCALL_RET(RaCALL_RET),
    .Rb(decoder_1_out0), .Rd(decoder_2_out0), .ENABLE(R0), .CLOCK(CLOCK), .out_10(R0_2));
  _8_16_bit_register u_R1 (
    .HI_LO(LO_HI), ._16(_16), .HI_LO_AND_16_8(SEL), .RbCALL_RET(RbCALL_RET), .RaCALL_RET(RaCALL_RET),
    .Rb(decoder_1_out1), .Rd(decoder_2_out1), .ENABLE(R1), .CLOCK(CLOCK), .out_10(R1_2));
  _8_16_bit_register u_R2 (
    .HI_LO(LO_HI), ._16(_16), .HI_LO_AND_16_8(SEL), .RbCALL_RET(RbCALL_RET), .RaCALL_RET(RaCALL_RET),
    .Rb(decoder_1_out2), .Rd(decoder_2_out2), .ENABLE(R2), .CLOCK(CLOCK), .out_10(R2_2));
  _8_16_bit_register u_R3 (
    .HI_LO(LO_HI), ._16(_16), .HI_LO_AND_16_8(SEL), .RbCALL_RET(RbCALL_RET), .RaCALL_RET(RaCALL_RET),
    .Rb(decoder_1_out3), .Rd(decoder_2_out3), .ENABLE(R3), .CLOCK(CLOCK), .out_10(R3_2));
endmodule

module R4_R7 (
  input  [7:0] LO_HI,
  input  [15:0] _16,
  input  [5:0] SEL,
  input  R4,
  input  R5,
  input  R6,
  input  R7,
  input  [15:0] RbCALL_RET,
  input  CLOCK,
  input  [15:0] RaCALL_RET,
  input  [7:0] Rb_AND_Ra,
  output [15:0] out_12,
  output [15:0] out_13,
  output [15:0] out_14,
  output [15:0] out_15
);

  wire decoder_1_out4, decoder_1_out5, decoder_1_out6, decoder_1_out7, decoder_2_out4, decoder_2_out5,
       decoder_2_out6, decoder_2_out7;

  Decoder #(.select(4)) decoder_1 (
    .out4(decoder_1_out4), .out5(decoder_1_out5), .out6(decoder_1_out6), .out7(decoder_1_out7),
    .sel(Rb_AND_Ra[3:0]));  // open: out0, out1, out2, out3, out8, out9, out10, out11, out12, out13, out14, out15, en
  Decoder #(.select(4)) decoder_2 (
    .out4(decoder_2_out4), .out5(decoder_2_out5), .out6(decoder_2_out6), .out7(decoder_2_out7),
    .sel(Rb_AND_Ra[7:4]));  // open: out0, out1, out2, out3, out8, out9, out10, out11, out12, out13, out14, out15, en
  _8_16_bit_register u_R4 (
    .HI_LO(LO_HI), ._16(_16), .HI_LO_AND_16_8(SEL), .RbCALL_RET(RbCALL_RET), .RaCALL_RET(RaCALL_RET),
    .Rb(decoder_1_out4), .Rd(decoder_2_out4), .ENABLE(R4), .CLOCK(CLOCK), .out_10(out_12));
  _8_16_bit_register u_R5 (
    .HI_LO(LO_HI), ._16(_16), .HI_LO_AND_16_8(SEL), .RbCALL_RET(RbCALL_RET), .RaCALL_RET(RaCALL_RET),
    .Rb(decoder_1_out5), .Rd(decoder_2_out5), .ENABLE(R5), .CLOCK(CLOCK), .out_10(out_13));
  _8_16_bit_register u_R6 (
    .HI_LO(LO_HI), ._16(_16), .HI_LO_AND_16_8(SEL), .RbCALL_RET(RbCALL_RET), .RaCALL_RET(RaCALL_RET),
    .Rb(decoder_1_out6), .Rd(decoder_2_out6), .ENABLE(R6), .CLOCK(CLOCK), .out_10(out_14));
  _8_16_bit_register u_R7 (
    .HI_LO(LO_HI), ._16(_16), .HI_LO_AND_16_8(SEL), .RbCALL_RET(RbCALL_RET), .RaCALL_RET(RaCALL_RET),
    .Rb(decoder_1_out7), .Rd(decoder_2_out7), .ENABLE(R7), .CLOCK(CLOCK), .out_10(out_15));
endmodule

module R8_R15 (
  input  [7:0] LO_HI,
  input  [15:0] _16,
  input  [5:0] SEL,
  input  R8,
  input  R9,
  input  R10,
  input  R11,
  input  R12,
  input  R13,
  input  R14,
  input  R15,
  input  CLOCK,
  input  [15:0] RbCALL_RET,
  input  [15:0] RaCALL_RET,
  input  [15:0] FPCALL_RET,
  input  [7:0] Rb_AND_Ra,
  output [15:0] out_17,
  output [15:0] out_18,
  output [15:0] out_19,
  output [15:0] out_20,
  output [15:0] out_21,
  output [15:0] out_22,
  output [15:0] out_23,
  output [15:0] out_24
);

  R8_R11 R8_R11 (
    .LO_HI(LO_HI), ._16(_16), .SEL(SEL), .R8(R8), .R9(R9), .R10(R10), .R11(R11), .RbCALL_RET(RbCALL_RET),
    .RaCALL_RET(RaCALL_RET), .Rb_AND_Ra(Rb_AND_Ra), .CLOCK(CLOCK), .R8_2(out_17), .R9_2(out_18),
    .R10_2(out_19), .R11_2(out_20));
  R12_R15 R12_15 (
    .LO_HI(LO_HI), ._16(_16), .SEL(SEL), .R12(R12), .R13(R13), .R14(R14), .R15(R15), .RbCALL_RET(RbCALL_RET),
    .RaCALL_RET(RaCALL_RET), .FPCALL_RET(FPCALL_RET), .Rb_AND_Ra(Rb_AND_Ra), .CLOCK(CLOCK), .R12_2(out_21),
    .R13_2(out_22), .R14_2(out_23), .R15_2(out_24));
endmodule

module R8_R11 (
  input  [7:0] LO_HI,
  input  [15:0] _16,
  input  [5:0] SEL,
  input  R8,
  input  R9,
  input  R10,
  input  R11,
  input  [15:0] RbCALL_RET,
  input  CLOCK,
  input  [15:0] RaCALL_RET,
  input  [7:0] Rb_AND_Ra,
  output [15:0] R8_2,
  output [15:0] R9_2,
  output [15:0] R10_2,
  output [15:0] R11_2
);

  wire decoder_1_out8, decoder_1_out9, decoder_1_out10, decoder_1_out11, decoder_2_out8, decoder_2_out9,
       decoder_2_out10, decoder_2_out11;

  Decoder #(.select(4)) decoder_1 (
    .out8(decoder_1_out8), .out9(decoder_1_out9), .out10(decoder_1_out10), .out11(decoder_1_out11),
    .sel(Rb_AND_Ra[3:0]));  // open: out0, out1, out2, out3, out4, out5, out6, out7, out12, out13, out14, out15, en
  Decoder #(.select(4)) decoder_2 (
    .out8(decoder_2_out8), .out9(decoder_2_out9), .out10(decoder_2_out10), .out11(decoder_2_out11),
    .sel(Rb_AND_Ra[7:4]));  // open: out0, out1, out2, out3, out4, out5, out6, out7, out12, out13, out14, out15, en
  _8_16_bit_register u_R8 (
    .HI_LO(LO_HI), ._16(_16), .HI_LO_AND_16_8(SEL), .RbCALL_RET(RbCALL_RET), .RaCALL_RET(RaCALL_RET),
    .Rb(decoder_1_out8), .Rd(decoder_2_out8), .ENABLE(R8), .CLOCK(CLOCK), .out_10(R8_2));
  _8_16_bit_register u_R9 (
    .HI_LO(LO_HI), ._16(_16), .HI_LO_AND_16_8(SEL), .RbCALL_RET(RbCALL_RET), .RaCALL_RET(RaCALL_RET),
    .Rb(decoder_1_out9), .Rd(decoder_2_out9), .ENABLE(R9), .CLOCK(CLOCK), .out_10(R9_2));
  _8_16_bit_register u_R10 (
    .HI_LO(LO_HI), ._16(_16), .HI_LO_AND_16_8(SEL), .RbCALL_RET(RbCALL_RET), .RaCALL_RET(RaCALL_RET),
    .Rb(decoder_1_out10), .Rd(decoder_2_out10), .ENABLE(R10), .CLOCK(CLOCK), .out_10(R10_2));
  _8_16_bit_register u_R11 (
    .HI_LO(LO_HI), ._16(_16), .HI_LO_AND_16_8(SEL), .RbCALL_RET(RbCALL_RET), .RaCALL_RET(RaCALL_RET),
    .Rb(decoder_1_out11), .Rd(decoder_2_out11), .ENABLE(R11), .CLOCK(CLOCK), .out_10(R11_2));
endmodule

module R12_R15 (
  input  [7:0] LO_HI,
  input  [15:0] _16,
  input  [5:0] SEL,
  input  R12,
  input  R13,
  input  R14,
  input  R15,
  input  [15:0] RbCALL_RET,
  input  CLOCK,
  input  [15:0] RaCALL_RET,
  input  [15:0] FPCALL_RET,
  input  [7:0] Rb_AND_Ra,
  output [15:0] R12_2,
  output [15:0] R13_2,
  output [15:0] R14_2,
  output [15:0] R15_2
);

  wire decoder_1_out12, decoder_1_out13, decoder_1_out15, decoder_2_out12, decoder_2_out13, decoder_2_out15;

  Decoder #(.select(4)) decoder_1 (
    .out12(decoder_1_out12), .out13(decoder_1_out13), .out15(decoder_1_out15), .sel(Rb_AND_Ra[3:0]));  // open: out0, out1, out2, out3, out4, out5, out6, out7, out8, out9, out10, out11, out14, en
  Decoder #(.select(4)) decoder_2 (
    .out12(decoder_2_out12), .out13(decoder_2_out13), .out15(decoder_2_out15), .sel(Rb_AND_Ra[7:4]));  // open: out0, out1, out2, out3, out4, out5, out6, out7, out8, out9, out10, out11, out14, en
  _8_16_bit_register u_R12 (
    .HI_LO(LO_HI), ._16(_16), .HI_LO_AND_16_8(SEL), .RbCALL_RET(RbCALL_RET), .RaCALL_RET(RaCALL_RET),
    .Rb(decoder_1_out12), .Rd(decoder_2_out12), .ENABLE(R12), .CLOCK(CLOCK), .out_10(R12_2));
  _8_16_bit_register u_R13 (
    .HI_LO(LO_HI), ._16(_16), .HI_LO_AND_16_8(SEL), .RbCALL_RET(RbCALL_RET), .RaCALL_RET(RaCALL_RET),
    .Rb(decoder_1_out13), .Rd(decoder_2_out13), .ENABLE(R13), .CLOCK(CLOCK), .out_10(R13_2));
  FPReg R14FP (
    .HI_LO(LO_HI), ._16(_16), .HI_LO_AND_16_8(SEL), .NEWFP(FPCALL_RET), .ENABLE(R14), .CLOCK(CLOCK),
    .out_7(R14_2));
  _8_16_bit_register u_R15 (
    .HI_LO(LO_HI), ._16(_16), .HI_LO_AND_16_8(SEL), .RbCALL_RET(RbCALL_RET), .RaCALL_RET(RaCALL_RET),
    .Rb(decoder_1_out15), .Rd(decoder_2_out15), .ENABLE(R15), .CLOCK(CLOCK), .out_10(R15_2));
endmodule

module LOAD_STORE (
  input  [15:0] Rb_DATA,
  input  [15:0] COMMAND,
  input  CLOCK,
  input  [15:0] INPUT_MEMORY_DATA,
  input  [15:0] Rd_DATA,
  output [3:0] Rb_REGISTER,
  output [3:0] Rd_REGISTER,
  output [15:0] retrieval_M_position,
  output LD,
  output [15:0] OUTPUT_DATA,
  output S_L,
  output [15:0] OUTPUT_M_LOC
);

  wire adder_1_cout, and_1_out, d_ff_1_q, d_ff_2_q, not_1_out, or_1_out;
  wire [1:0] LOAD_out;

  and LOAD (LOAD_out[0], ~COMMAND[13], COMMAND[14], ~COMMAND[15]);  // AND_Gate
  and STORE (LOAD_out[1], COMMAND[13], COMMAND[14], ~COMMAND[15]);  // AND_Gate
  D_Flip_Flop d_ff_1 (.clk(CLOCK), .D(COMMAND[13]), .Q(d_ff_1_q));  // open: Qn, preset, en, reset
  Adder #(.width(16)) adder_1 (
    .a(Rb_DATA), .b({{11{1'b0}}, COMMAND[12], COMMAND[7:4]}), .out(retrieval_M_position), .cin(1'b0),
    .cout(adder_1_cout));
  D_Flip_Flop d_ff_2 (.clk(CLOCK), .D(d_ff_1_q), .Q(d_ff_2_q));  // open: Qn, preset, en, reset
  or or_1 (or_1_out, LOAD_out[0], LOAD_out[1]);
  Multiplexer #(.select(2), .width(16)) multiplexer_1 (
    .in1(INPUT_MEMORY_DATA), .in2(Rd_DATA), .out(OUTPUT_DATA), .sel(LOAD_out));  // open: in0, in3, en
  Multiplexer #(.width(16)) multiplexer_2 (
    .in1(INPUT_MEMORY_DATA), .out(OUTPUT_M_LOC), .sel(1'b1), .en(LOAD_out[0]));  // open: in0
  and and_1 (and_1_out, d_ff_2_q, LOAD_out[0]);
  not not_1 (not_1_out, or_1_out);
  Multiplexer multiplexer_3 (.in0(not_1_out), .in1(and_1_out), .out(LD), .sel(and_1_out), .en(or_1_out));

  assign Rb_REGISTER = COMMAND[3:0];
  assign Rd_REGISTER = COMMAND[11:8];
  assign S_L = COMMAND[13];
endmodule

module LOADF (
  input  [3:0] _15ORIG,
  input  [15:0] LOADRESULT,
  output LS,
  output LZ
);

  wire and_1_out, nor_1_out;

  and and_1 (and_1_out, ~_15ORIG[1], _15ORIG[2], ~_15ORIG[3]);  // AND_Gate
  Multiplexer multiplexer_1 (.in0(1'b0), .in1(LOADRESULT[15]), .out(LS), .sel(and_1_out));  // open: en
  Multiplexer multiplexer_2 (.in0(1'b0), .in1(nor_1_out), .out(LZ), .sel(and_1_out));  // open: en
  nor nor_1 (nor_1_out, LOADRESULT[0], LOADRESULT[1], LOADRESULT[2], LOADRESULT[3], LOADRESULT[4], LOADRESULT[5], LOADRESULT[6], LOADRESULT[7], LOADRESULT[8], LOADRESULT[9], LOADRESULT[10], LOADRESULT[11], LOADRESULT[12], LOADRESULT[13], LOADRESULT[14], LOADRESULT[15]);
endmodule

module RDregisterSEL (
  input  [3:0] RDSEL1,
  input  [3:0] RDSEL2,
  input  [3:0] RbREG,
  input  [3:0] RdREG,
  input  [3:0] _7ORIG,
  input  [3:0] _12_15ORIG,
  output [3:0] RDSEL1_2,
  output [3:0] RDSEL2_2
);

  wire and_1_out, and_2_out, and_3_out, or_1_out;
  wire [3:0] multiplexer_1_out;

  Multiplexer #(.width(4)) multiplexer_1 (
    .in0(RdREG), .in1(_7ORIG), .out(multiplexer_1_out), .sel(and_3_out));  // open: en
  and and_1 (and_1_out, _12_15ORIG[2], ~_12_15ORIG[3]);  // AND_Gate
  and and_2 (and_2_out, ~_12_15ORIG[1], ~_12_15ORIG[2], ~_12_15ORIG[3]);  // AND_Gate
  and and_3 (and_3_out, ~_12_15ORIG[0], _12_15ORIG[1], ~_12_15ORIG[2], ~_12_15ORIG[3]);  // AND_Gate
  Multiplexer #(.width(4)) multiplexer_2 (.in0(RDSEL1), .in1(RbREG), .out(RDSEL1_2), .sel(or_1_out));  // open: en
  Multiplexer #(.width(4)) multiplexer_3 (
    .in0(RDSEL2), .in1(multiplexer_1_out), .out(RDSEL2_2), .sel(or_1_out));  // open: en
  or or_1 (or_1_out, and_1_out, and_2_out, and_3_out);
endmodule

module BRANCHES (
  input  O,
  input  Z,
  input  C,
  input  S,
  input  CB,
  input  [15:0] RDBr,
  input  [15:0] PC,
  input  [15:0] CMD,
  output [15:0] PC_PLACE,
  output MOVE_PC
);

  wire and_1_out, multiplexer_1_out, not_1_out, not_2_out, not_3_out, not_4_out, not_5_out, not_6_out,
       not_7_out, or_1_out, or_2_out, xor_1_out;

  altBR altbr_1 (.RDBr(RDBr), .PC(PC), ._0_7BITS(CMD[7:0]), .Rb_O(CMD[12]), .PC_PLACE(PC_PLACE));
  and and_1 (and_1_out, ~CMD[13], ~CMD[14], ~CMD[15]);  // AND_Gate
  not not_1 (not_1_out, C);
  or or_1 (or_1_out, Z, not_1_out);
  not not_2 (not_2_out, or_1_out);
  xor xor_1 (xor_1_out, O, S);
  not not_3 (not_3_out, xor_1_out);
  or or_2 (or_2_out, xor_1_out, Z);
  not not_4 (not_4_out, or_2_out);
  not not_5 (not_5_out, S);
  not not_6 (not_6_out, O);
  not not_7 (not_7_out, Z);
  Multiplexer #(.select(4)) multiplexer_1 (
    .in0(1'b1), .in2(xor_1_out), .in3(not_3_out), .in4(or_2_out), .in5(not_4_out), .in6(or_1_out),
    .in7(not_2_out), .in8(Z), .in9(not_7_out), .in10(C), .in11(not_1_out), .in12(S), .in13(not_5_out),
    .in14(O), .in15(not_6_out), .out(multiplexer_1_out), .sel(CMD[11:8]));  // open: in1, en
  and and_2 (MOVE_PC, multiplexer_1_out, and_1_out);

  // Other names for the same wires on the sheet: Rb_O = CMD[12]; CO = C; OVF = O; SIGN = S; ZERO = Z

  // Notes on the sheet:
  //   BC/R
  //   BNC/R
  //   BULE/R
  //   BUG/R
  //   BS/R
  //   BNS/R
  //   BV/R
  //   BL/R
  //   BGE/R
  //   BLE/R
  //   BG/R
  //   BZ/R
  //   BNZ/R
  //   BR/R
  //   BNV/R
endmodule

module SIGN (
  input  [15:0] RESULT,
  input  NS,
  input  Arth,
  input  SIGN,
  input  LS,
  output SIGN_2
);

  wire and_1_out;

  and and_1 (and_1_out, ~NS, RESULT[15], Arth);  // AND_Gate
  or or_1 (SIGN_2, and_1_out, SIGN, LS);
endmodule

module ZERO (
  input  ZERO,
  input  [15:0] RESULT,
  input  NS,
  input  Arth,
  input  LZ,
  output ZERO_2
);

  wire and_1_out, nor_1_out;

  and and_1 (and_1_out, ~NS, nor_1_out, Arth);  // AND_Gate
  nor nor_1 (nor_1_out, RESULT[0], RESULT[1], RESULT[2], RESULT[3], RESULT[4], RESULT[5], RESULT[6], RESULT[7], RESULT[8], RESULT[9], RESULT[10], RESULT[11], RESULT[12], RESULT[13], RESULT[14], RESULT[15]);
  or or_1 (ZERO_2, and_1_out, ZERO, LZ);
endmodule

module OF (
  input  [15:0] in_1,
  input  [15:0] in_2,
  input  [15:0] in_3,
  input  in_4,
  input  in_5,
  output out_6
);

  wire and_1_out, and_2_out;

  and and_1 (and_1_out, ~in_3[15], in_1[15], in_2[15], in_4);  // AND_Gate
  and and_2 (and_2_out, in_3[15], ~in_1[15], ~in_2[15], in_4);  // AND_Gate
  or or_1 (out_6, and_1_out, and_2_out, in_5);
endmodule

module altBR (
  input  [15:0] RDBr,
  input  [15:0] PC,
  input  Rb_O,
  input  [7:0] _0_7BITS,
  output [15:0] PC_PLACE
);

  wire [15:0] adder_1_out;

  Adder #(.width(16)) adder_1 (.a(PC), .b({{8{1'b0}}, _0_7BITS}), .out(adder_1_out));  // open: cin, cout
  Multiplexer #(.width(16)) multiplexer_1 (.in0(adder_1_out), .in1(RDBr), .out(PC_PLACE), .sel(Rb_O));  // open: en
endmodule

// ADD/SUB
module SIGNED_ADD_SUB (
  input  ADD_SUB,
  input  C,
  input  CB,
  input  [15:0] _4_Bit_input__1,
  input  [15:0] _4_Bit_input__2,
  output Carry_Out,
  output [15:0] out_7
);

  wire and_1_out, mfa_1_carry_out, mfa_2_carry_out, mfa_3_carry_out, mfa_4_carry_out, mfa_5_carry_out,
       mfa_6_carry_out, mfa_7_carry_out, mfa_8_carry_out, mfa_9_carry_out, mfa_10_carry_out,
       mfa_11_carry_out, mfa_12_carry_out, mfa_13_carry_out, mfa_14_carry_out, mfa_15_carry_out,
       multiplexer_1_out, not_1_out, undriven, xor_1_out, xor_2_out, xor_3_out, xor_4_out, xor_5_out,
       xor_6_out, xor_7_out, xor_8_out, xor_9_out, xor_10_out, xor_11_out, xor_12_out, xor_13_out,
       xor_14_out, xor_15_out, xor_16_out;

  not not_1 (not_1_out, ADD_SUB);
  and and_1 (and_1_out, ~CB, C);  // AND_Gate
  Multiplexer multiplexer_1 (.in0(ADD_SUB), .in1(and_1_out), .out(multiplexer_1_out), .sel(not_1_out));  // open: en
  xor xor_1 (xor_1_out, _4_Bit_input__2[1], ADD_SUB);
  xor xor_2 (xor_2_out, _4_Bit_input__2[0], ADD_SUB);
  MFA mfa_1 (
    .Carry_In(mfa_2_carry_out), .A(_4_Bit_input__1[1]), .B(xor_1_out), .Sum(out_7[1]),
    .Carry_out(mfa_1_carry_out));
  MFA mfa_2 (
    .Carry_In(multiplexer_1_out), .A(_4_Bit_input__1[0]), .B(xor_2_out), .Sum(out_7[0]),
    .Carry_out(mfa_2_carry_out));
  xor xor_3 (xor_3_out, _4_Bit_input__2[2], ADD_SUB);
  MFA mfa_3 (
    .Carry_In(mfa_1_carry_out), .A(_4_Bit_input__1[2]), .B(xor_3_out), .Sum(out_7[2]),
    .Carry_out(mfa_3_carry_out));
  xor xor_4 (xor_4_out, _4_Bit_input__2[3], ADD_SUB);
  MFA mfa_4 (
    .Carry_In(mfa_3_carry_out), .A(_4_Bit_input__1[3]), .B(xor_4_out), .Sum(out_7[3]),
    .Carry_out(mfa_4_carry_out));
  xor xor_5 (xor_5_out, _4_Bit_input__2[5], ADD_SUB);
  xor xor_6 (xor_6_out, _4_Bit_input__2[4], ADD_SUB);
  MFA mfa_5 (
    .Carry_In(mfa_6_carry_out), .A(_4_Bit_input__1[5]), .B(xor_5_out), .Sum(out_7[5]),
    .Carry_out(mfa_5_carry_out));
  MFA mfa_6 (
    .Carry_In(mfa_4_carry_out), .A(_4_Bit_input__1[4]), .B(xor_6_out), .Sum(out_7[4]),
    .Carry_out(mfa_6_carry_out));
  xor xor_7 (xor_7_out, _4_Bit_input__2[6], ADD_SUB);
  MFA mfa_7 (
    .Carry_In(mfa_5_carry_out), .A(_4_Bit_input__1[6]), .B(xor_7_out), .Sum(out_7[6]),
    .Carry_out(mfa_7_carry_out));
  xor xor_8 (xor_8_out, _4_Bit_input__2[7], ADD_SUB);
  MFA mfa_8 (
    .Carry_In(mfa_7_carry_out), .A(_4_Bit_input__1[7]), .B(xor_8_out), .Sum(out_7[7]),
    .Carry_out(mfa_8_carry_out));
  xor xor_9 (xor_9_out, _4_Bit_input__2[9], ADD_SUB);
  xor xor_10 (xor_10_out, _4_Bit_input__2[8], ADD_SUB);
  MFA mfa_9 (
    .Carry_In(mfa_8_carry_out), .A(_4_Bit_input__1[8]), .B(xor_10_out), .Sum(out_7[8]),
    .Carry_out(mfa_9_carry_out));
  MFA mfa_10 (
    .Carry_In(mfa_9_carry_out), .A(_4_Bit_input__1[9]), .B(xor_9_out), .Sum(out_7[9]),
    .Carry_out(mfa_10_carry_out));
  xor xor_11 (xor_11_out, _4_Bit_input__2[10], ADD_SUB);
  MFA mfa_11 (
    .Carry_In(mfa_10_carry_out), .A(_4_Bit_input__1[10]), .B(xor_11_out), .Sum(out_7[10]),
    .Carry_out(mfa_11_carry_out));
  xor xor_12 (xor_12_out, _4_Bit_input__2[11], ADD_SUB);
  MFA mfa_12 (
    .Carry_In(mfa_11_carry_out), .A(_4_Bit_input__1[11]), .B(xor_12_out), .Sum(out_7[11]),
    .Carry_out(mfa_12_carry_out));
  xor xor_13 (xor_13_out, _4_Bit_input__2[13], ADD_SUB);
  xor xor_14 (xor_14_out, _4_Bit_input__2[12], ADD_SUB);
  MFA mfa_13 (
    .Carry_In(mfa_14_carry_out), .A(_4_Bit_input__1[13]), .B(xor_13_out), .Sum(out_7[13]),
    .Carry_out(mfa_13_carry_out));
  MFA mfa_14 (
    .Carry_In(mfa_12_carry_out), .A(_4_Bit_input__1[12]), .B(xor_14_out), .Sum(out_7[12]),
    .Carry_out(mfa_14_carry_out));
  xor xor_15 (xor_15_out, _4_Bit_input__2[14], ADD_SUB);
  MFA mfa_15 (
    .Carry_In(mfa_13_carry_out), .A(_4_Bit_input__1[14]), .B(xor_15_out), .Sum(out_7[14]),
    .Carry_out(mfa_15_carry_out));
  xor xor_16 (xor_16_out, _4_Bit_input__2[15], ADD_SUB);
  MFA mfa_16 (
    .Carry_In(mfa_15_carry_out), .A(_4_Bit_input__1[15]), .B(xor_16_out), .Sum(out_7[15]),
    .Carry_out(Carry_Out));
  // XOR_Gate xor_17 has open pins: in3=undriven, out=open

  // Other names for the same wires on the sheet: A0 = _4_Bit_input__1[0]; A1 = _4_Bit_input__1[1];
  //   A2 = _4_Bit_input__1[2]; A3 = _4_Bit_input__1[3]; A4 = _4_Bit_input__1[4]; A5 = _4_Bit_input__1[5];
  //   A6 = _4_Bit_input__1[6]; A7 = _4_Bit_input__1[7]; A8 = _4_Bit_input__1[8]; A9 = _4_Bit_input__1[9];
  //   A10 = _4_Bit_input__1[10]; A11 = _4_Bit_input__1[11]; A12 = _4_Bit_input__1[12]; A13 = _4_Bit_input__1[13];
  //   A14 = _4_Bit_input__1[14]; A15 = _4_Bit_input__1[15]; B0 = _4_Bit_input__2[0]; B1 = _4_Bit_input__2[1];
  //   B2 = _4_Bit_input__2[2]; B3 = _4_Bit_input__2[3]; B4 = _4_Bit_input__2[4]; B5 = _4_Bit_input__2[5];
  //   B6 = _4_Bit_input__2[6]; B7 = _4_Bit_input__2[7]; B8 = _4_Bit_input__2[8]; B9 = _4_Bit_input__2[9];
  //   B10 = _4_Bit_input__2[10]; B11 = _4_Bit_input__2[11]; B12 = _4_Bit_input__2[12]; B13 = _4_Bit_input__2[13];
  //   B14 = _4_Bit_input__2[14]; B15 = _4_Bit_input__2[15]

  // Notes on the sheet:
  //   +
  //   This xor gate is to ensure the sign is correct.
endmodule

module MFA (
  input  A,
  input  B,
  input  Carry_In,
  output Carry_out,
  output Sum
);

  wire and_1_out, and_2_out, xor_1_out;

  xor xor_1 (xor_1_out, A, B);
  and and_1 (and_1_out, B, A);
  xor xor_2 (Sum, xor_1_out, Carry_In);
  and and_2 (and_2_out, xor_1_out, Carry_In);
  or or_1 (Carry_out, and_1_out, and_2_out);
endmodule

module test (
  input  ADD_SUB,
  input  C,
  input  CB,
  input  [15:0] _4_Bit_input__1,
  input  [15:0] _4_Bit_input__2,
  output Carry_Out,
  output [15:0] out_7
);

  wire and_1_out, mfa_1_carry_out, mfa_2_carry_out, mfa_3_carry_out, mfa_4_carry_out, mfa_5_carry_out,
       mfa_6_carry_out, mfa_7_carry_out, mfa_8_carry_out, mfa_9_carry_out, mfa_10_carry_out,
       mfa_11_carry_out, mfa_12_carry_out, mfa_13_carry_out, mfa_14_carry_out, mfa_15_carry_out,
       multiplexer_1_out, not_1_out, undriven, xor_1_out, xor_2_out, xor_3_out, xor_4_out, xor_5_out,
       xor_6_out, xor_7_out, xor_8_out, xor_9_out, xor_10_out, xor_11_out, xor_12_out, xor_13_out,
       xor_14_out, xor_15_out, xor_16_out;

  // NAND_Gate nand_1 has open pins: in1=CB, in3=C, out=open
  not not_1 (not_1_out, ADD_SUB);
  and and_1 (and_1_out, ~CB, C);  // AND_Gate
  Multiplexer multiplexer_1 (.in0(ADD_SUB), .in1(and_1_out), .out(multiplexer_1_out), .sel(not_1_out));  // open: en
  xor xor_1 (xor_1_out, _4_Bit_input__2[1], ADD_SUB);
  xor xor_2 (xor_2_out, _4_Bit_input__2[0], ADD_SUB);
  MFA mfa_1 (
    .Carry_In(mfa_2_carry_out), .A(_4_Bit_input__1[1]), .B(xor_1_out), .Sum(out_7[1]),
    .Carry_out(mfa_1_carry_out));
  MFA mfa_2 (
    .Carry_In(multiplexer_1_out), .A(_4_Bit_input__1[0]), .B(xor_2_out), .Sum(out_7[0]),
    .Carry_out(mfa_2_carry_out));
  xor xor_3 (xor_3_out, _4_Bit_input__2[2], ADD_SUB);
  MFA mfa_3 (
    .Carry_In(mfa_1_carry_out), .A(_4_Bit_input__1[2]), .B(xor_3_out), .Sum(out_7[2]),
    .Carry_out(mfa_3_carry_out));
  xor xor_4 (xor_4_out, _4_Bit_input__2[3], ADD_SUB);
  MFA mfa_4 (
    .Carry_In(mfa_3_carry_out), .A(_4_Bit_input__1[3]), .B(xor_4_out), .Sum(out_7[3]),
    .Carry_out(mfa_4_carry_out));
  xor xor_5 (xor_5_out, _4_Bit_input__2[5], ADD_SUB);
  xor xor_6 (xor_6_out, _4_Bit_input__2[4], ADD_SUB);
  MFA mfa_5 (
    .Carry_In(mfa_4_carry_out), .A(_4_Bit_input__1[4]), .B(xor_6_out), .Sum(out_7[4]),
    .Carry_out(mfa_5_carry_out));
  MFA mfa_6 (
    .Carry_In(mfa_5_carry_out), .A(_4_Bit_input__1[5]), .B(xor_5_out), .Sum(out_7[5]),
    .Carry_out(mfa_6_carry_out));
  xor xor_7 (xor_7_out, _4_Bit_input__2[6], ADD_SUB);
  MFA mfa_7 (
    .Carry_In(mfa_6_carry_out), .A(_4_Bit_input__1[6]), .B(xor_7_out), .Sum(out_7[6]),
    .Carry_out(mfa_7_carry_out));
  xor xor_8 (xor_8_out, _4_Bit_input__2[7], ADD_SUB);
  MFA mfa_8 (
    .Carry_In(mfa_7_carry_out), .A(_4_Bit_input__1[7]), .B(xor_8_out), .Sum(out_7[7]),
    .Carry_out(mfa_8_carry_out));
  xor xor_9 (xor_9_out, _4_Bit_input__2[9], ADD_SUB);
  xor xor_10 (xor_10_out, _4_Bit_input__2[8], ADD_SUB);
  MFA mfa_9 (
    .Carry_In(mfa_8_carry_out), .A(_4_Bit_input__1[8]), .B(xor_10_out), .Sum(out_7[8]),
    .Carry_out(mfa_9_carry_out));
  MFA mfa_10 (
    .Carry_In(mfa_9_carry_out), .A(_4_Bit_input__1[9]), .B(xor_9_out), .Sum(out_7[9]),
    .Carry_out(mfa_10_carry_out));
  xor xor_11 (xor_11_out, _4_Bit_input__2[10], ADD_SUB);
  MFA mfa_11 (
    .Carry_In(mfa_10_carry_out), .A(_4_Bit_input__1[10]), .B(xor_11_out), .Sum(out_7[10]),
    .Carry_out(mfa_11_carry_out));
  xor xor_12 (xor_12_out, _4_Bit_input__2[11], ADD_SUB);
  MFA mfa_12 (
    .Carry_In(mfa_11_carry_out), .A(_4_Bit_input__1[11]), .B(xor_12_out), .Sum(out_7[11]),
    .Carry_out(mfa_12_carry_out));
  xor xor_13 (xor_13_out, _4_Bit_input__2[13], ADD_SUB);
  xor xor_14 (xor_14_out, _4_Bit_input__2[12], ADD_SUB);
  MFA mfa_13 (
    .Carry_In(mfa_12_carry_out), .A(_4_Bit_input__1[12]), .B(xor_14_out), .Sum(out_7[12]),
    .Carry_out(mfa_13_carry_out));
  MFA mfa_14 (
    .Carry_In(mfa_13_carry_out), .A(_4_Bit_input__1[13]), .B(xor_13_out), .Sum(out_7[13]),
    .Carry_out(mfa_14_carry_out));
  xor xor_15 (xor_15_out, _4_Bit_input__2[14], ADD_SUB);
  MFA mfa_15 (
    .Carry_In(mfa_14_carry_out), .A(_4_Bit_input__1[14]), .B(xor_15_out), .Sum(out_7[14]),
    .Carry_out(mfa_15_carry_out));
  xor xor_16 (xor_16_out, _4_Bit_input__2[15], ADD_SUB);
  MFA mfa_16 (
    .Carry_In(mfa_15_carry_out), .A(_4_Bit_input__1[15]), .B(xor_16_out), .Sum(out_7[15]),
    .Carry_out(Carry_Out));
  // XOR_Gate xor_17 has open pins: in3=undriven, out=open

  // Other names for the same wires on the sheet: A0 = _4_Bit_input__1[0]; A1 = _4_Bit_input__1[1];
  //   A2 = _4_Bit_input__1[2]; A3 = _4_Bit_input__1[3]; A4 = _4_Bit_input__1[4]; A5 = _4_Bit_input__1[5];
  //   A6 = _4_Bit_input__1[6]; A7 = _4_Bit_input__1[7]; A8 = _4_Bit_input__1[8]; A9 = _4_Bit_input__1[9];
  //   A10 = _4_Bit_input__1[10]; A11 = _4_Bit_input__1[11]; A12 = _4_Bit_input__1[12]; A13 = _4_Bit_input__1[13];
  //   A14 = _4_Bit_input__1[14]; A15 = _4_Bit_input__1[15]; B0 = _4_Bit_input__2[0]; B1 = _4_Bit_input__2[1];
  //   B2 = _4_Bit_input__2[2]; B3 = _4_Bit_input__2[3]; B4 = _4_Bit_input__2[4]; B5 = _4_Bit_input__2[5];
  //   B6 = _4_Bit_input__2[6]; B7 = _4_Bit_input__2[7]; B8 = _4_Bit_input__2[8]; B9 = _4_Bit_input__2[9];
  //   B10 = _4_Bit_input__2[10]; B11 = _4_Bit_input__2[11]; B12 = _4_Bit_input__2[12]; B13 = _4_Bit_input__2[13];
  //   B14 = _4_Bit_input__2[14]; B15 = _4_Bit_input__2[15]

  // Notes on the sheet:
  //   +
  //   This xor gate is to ensure the sign is correct.
endmodule
